// Logisim project projeto-guess-the-number.circ as structural Verilog: 9 circuits, main circuit main
module main (
  input  Confirmar,
  input  [3:0] Chute
);

  wire \guess_the_number_1_saída , n7_segmentos_full_1_a_2, n7_segmentos_full_1_b_2, n7_segmentos_full_1_c_2,
       n7_segmentos_full_1_d_2, n7_segmentos_full_1_e, n7_segmentos_full_1_f, n7_segmentos_full_1_g,
       Resetar_out;

  Button Resetar (.out(Resetar_out));
  // RGBLed #(.multibit("true")) rgbled_1: pin names not known; wires that end beside it: Confirmar
  Guess_the_number guess_the_number_1 (
    .Confirmar(Confirmar), .in_2(Resetar_out), .Chute(Chute), .\Saída (\guess_the_number_1_saída ));  // open: red, blue
  LED led_1 (.in(\guess_the_number_1_saída ));
  _7_segmentos_full u_7_segmentos_full_1 (
    .a_2(n7_segmentos_full_1_a_2), .A(Chute[3]), .B(Chute[2]), .C(Chute[1]), .D(Chute[0]),
    .b_2(n7_segmentos_full_1_b_2), .c_2(n7_segmentos_full_1_c_2), .d_2(n7_segmentos_full_1_d_2),
    .e(n7_segmentos_full_1_e), .f(n7_segmentos_full_1_f), .g(n7_segmentos_full_1_g));
  _7_Segment_Display u_7_segment_display_1 (
    .g(n7_segmentos_full_1_g), .f(n7_segmentos_full_1_f), .a(n7_segmentos_full_1_a_2),
    .b(n7_segmentos_full_1_b_2), .e(n7_segmentos_full_1_e), .d(n7_segmentos_full_1_d_2),
    .c(n7_segmentos_full_1_c_2));  // open: dp
endmodule

module diferenca (
  input  [3:0] B,
  input  [3:0] A,
  output [3:0] out_3
);

  wire subtrator_1_borrow_out, subtrator_1_diff, subtrator_2_borrow_out, subtrator_2_diff,
       subtrator_3_borrow_out, subtrator_3_diff, subtrator_4_borrow_out, subtrator_4_diff,
       subtrator_5_borrow_out, subtrator_5_diff, subtrator_6_borrow_out, subtrator_6_diff,
       subtrator_7_borrow_out, subtrator_7_diff, subtrator_8_diff;

  subtrator subtrator_1 (
    .A(A[0]), .B(B[0]), .Borrow_IN(1'b0), .DIFF(subtrator_1_diff), .Borrow_OUT(subtrator_1_borrow_out));
  subtrator subtrator_2 (
    .A(A[1]), .B(B[1]), .Borrow_IN(subtrator_1_borrow_out), .DIFF(subtrator_2_diff),
    .Borrow_OUT(subtrator_2_borrow_out));
  subtrator subtrator_3 (
    .A(A[2]), .B(B[2]), .Borrow_IN(subtrator_2_borrow_out), .DIFF(subtrator_3_diff),
    .Borrow_OUT(subtrator_3_borrow_out));
  subtrator subtrator_4 (
    .A(A[3]), .B(B[3]), .Borrow_IN(subtrator_3_borrow_out), .DIFF(subtrator_4_diff),
    .Borrow_OUT(subtrator_4_borrow_out));
  subtrator subtrator_5 (
    .A(B[0]), .B(A[0]), .Borrow_IN(1'b0), .DIFF(subtrator_5_diff), .Borrow_OUT(subtrator_5_borrow_out));
  subtrator subtrator_6 (
    .A(B[1]), .B(A[1]), .Borrow_IN(subtrator_5_borrow_out), .DIFF(subtrator_6_diff),
    .Borrow_OUT(subtrator_6_borrow_out));
  subtrator subtrator_7 (
    .A(B[2]), .B(A[2]), .Borrow_IN(subtrator_6_borrow_out), .DIFF(subtrator_7_diff),
    .Borrow_OUT(subtrator_7_borrow_out));
  subtrator subtrator_8 (
    .A(B[3]), .B(A[3]), .Borrow_IN(subtrator_7_borrow_out), .DIFF(subtrator_8_diff));  // open: Borrow_OUT
  multiplexador multiplexador_1 (
    .I0(subtrator_1_diff), .I1(subtrator_5_diff), .S(subtrator_4_borrow_out), .out_4(out_3[0]));
  multiplexador multiplexador_2 (
    .I0(subtrator_2_diff), .I1(subtrator_6_diff), .S(subtrator_4_borrow_out), .out_4(out_3[1]));
  multiplexador multiplexador_3 (
    .I0(subtrator_3_diff), .I1(subtrator_7_diff), .S(subtrator_4_borrow_out), .out_4(out_3[2]));
  multiplexador multiplexador_4 (
    .I0(subtrator_4_diff), .I1(subtrator_8_diff), .S(subtrator_4_borrow_out), .out_4(out_3[3]));
endmodule

module comparador (
  input  [3:0] in_1,
  input  [3:0] in_2,
  output out_3
);

  wire xnor_1_out, xnor_2_out, xnor_3_out, xnor_4_out;

  xnor xnor_1 (xnor_1_out, in_1[3], in_2[3]);
  xnor xnor_2 (xnor_2_out, in_1[2], in_2[2]);
  xnor xnor_3 (xnor_3_out, in_1[1], in_2[1]);
  xnor xnor_4 (xnor_4_out, in_1[0], in_2[0]);
  and and_1 (out_3, xnor_1_out, xnor_2_out, xnor_3_out, xnor_4_out);
endmodule

module Guess_the_number (
  input  Confirmar,
  input  in_2,
  input  [3:0] Chute,
  output [7:0] red,
  output [7:0] blue,
  output \Saída 
);

  wire comparador_out_3;
  wire [3:0] diferenca_out_3, random_1_out;
  wire [7:0] bit_extender_1_out, cores_1_s1, cores_1_s2;

  assign bit_extender_1_out = {{7{Confirmar}}, Confirmar};  // Bit_Extender bit_extender_1
  Random #(.width(4)) random_1 (.clk(in_2), .out(random_1_out));  // open: next, clr
  assign red = bit_extender_1_out & cores_1_s1;  // AND_Gate and_1, 8 bits wide
  Cores cores_1 (.a(diferenca_out_3), .S1(cores_1_s1), .S2(cores_1_s2));
  diferenca diferenca (.out_3(diferenca_out_3), .B(random_1_out), .A(Chute));
  comparador comparador (.in_1(random_1_out), .in_2(Chute), .out_3(comparador_out_3));
  assign blue = bit_extender_1_out & cores_1_s2;  // AND_Gate and_2, 8 bits wide
  and and_3 (\Saída , Confirmar, comparador_out_3);
endmodule

module Cores (
  input  [3:0] a,
  output [7:0] S1,
  output [7:0] S2
);

  not not_1 (S1[4], a[0]);
  not not_2 (S1[5], a[1]);
  not not_3 (S1[6], a[2]);
  not not_4 (S1[7], a[3]);

  assign S1[3:0] = 4'b0000;
  assign S2 = {a, 4'b0000};

  // Other names for the same wires on the sheet: NA0 = S1[4]; NA1 = S1[5]; NA2 = S1[6]; NA3 = S1[7]
endmodule

module subtrator (
  input  A,
  input  B,
  input  Borrow_IN,
  output DIFF,
  output Borrow_OUT
);

  wire and_1_out, and_2_out, and_3_out, xor_1_out;

  xor xor_1 (xor_1_out, A, B);
  and and_1 (and_1_out, B, Borrow_IN);
  and and_2 (and_2_out, ~A, Borrow_IN);  // AND_Gate
  and and_3 (and_3_out, ~A, B);  // AND_Gate
  xor xor_2 (DIFF, xor_1_out, Borrow_IN);
  or or_1 (Borrow_OUT, and_1_out, and_2_out, and_3_out);
endmodule

module multiplexador (
  input  I0,
  input  I1,
  input  S,
  output out_4
);

  wire and_1_out, and_2_out;

  and and_1 (and_1_out, I0, ~S);  // AND_Gate
  and and_2 (and_2_out, I1, S);
  or or_1 (out_4, and_1_out, and_2_out);
endmodule

module _7_segmentos (
  input  D,
  input  C,
  input  B,
  input  A,
  output a_2,
  output b_2,
  output c_2,
  output d_2,
  output e,
  output f,
  output g
);

  wire and_1_out, and_2_out, and_3_out, and_4_out, and_5_out, and_6_out, and_7_out, and_8_out, and_9_out,
       and_10_out, and_11_out, and_12_out, and_13_out, and_14_out, and_15_out, and_16_out, and_17_out,
       and_18_out, and_19_out, and_20_out, and_21_out, and_22_out, and_23_out, and_24_out, and_25_out,
       and_26_out, not_1_out, not_2_out, not_3_out, not_4_out, not_5_out, not_6_out, not_7_out, not_8_out,
       not_9_out, not_10_out, not_11_out, not_12_out, not_13_out, not_14_out, not_15_out;

  and and_1 (and_1_out, B, not_1_out);
  not not_1 (not_1_out, D);
  and and_2 (and_2_out, A, C, not_2_out);
  not not_2 (not_2_out, D);
  not not_3 (not_3_out, B);
  not not_4 (not_4_out, C);
  and and_3 (and_3_out, not_3_out, not_4_out, D);
  not not_5 (not_5_out, A);
  not not_6 (not_6_out, B);
  and and_4 (and_4_out, not_5_out, not_6_out, not_7_out);
  not not_7 (not_7_out, C);
  not not_8 (not_8_out, C);
  and and_5 (and_5_out, not_8_out, not_9_out);
  not not_9 (not_9_out, D);
  not not_10 (not_10_out, B);
  and and_6 (and_6_out, not_10_out, not_11_out);
  not not_11 (not_11_out, C);
  not not_12 (not_12_out, A);
  not not_13 (not_13_out, B);
  and and_7 (and_7_out, not_12_out, not_13_out, not_14_out);
  not not_14 (not_14_out, D);
  and and_8 (and_8_out, A, B, not_15_out);
  not not_15 (not_15_out, D);
  and and_9 (and_9_out, ~B, ~C);  // AND_Gate
  and and_10 (and_10_out, ~B, ~D);  // AND_Gate
  and and_11 (and_11_out, A, ~D);  // AND_Gate
  and and_12 (and_12_out, C, ~D);  // AND_Gate
  and and_13 (and_13_out, ~A, ~B, ~C);  // AND_Gate
  and and_14 (and_14_out, A, ~B, C, ~D);  // AND_Gate
  and and_15 (and_15_out, B, ~C, ~D);  // AND_Gate
  and and_16 (and_16_out, ~A, B, ~D);  // AND_Gate
  and and_17 (and_17_out, ~A, ~B, ~C);  // AND_Gate
  and and_18 (and_18_out, ~A, B, ~D);  // AND_Gate
  and and_19 (and_19_out, ~A, C, ~D);  // AND_Gate
  and and_20 (and_20_out, ~A, ~B, ~D);  // AND_Gate
  and and_21 (and_21_out, ~B, C, ~D);  // AND_Gate
  and and_22 (and_22_out, ~B, ~C, D);  // AND_Gate
  and and_23 (and_23_out, ~B, C, ~D);  // AND_Gate
  and and_24 (and_24_out, ~B, ~C, D);  // AND_Gate
  and and_25 (and_25_out, B, ~C, ~D);  // AND_Gate
  and and_26 (and_26_out, ~A, B, ~D);  // AND_Gate
  or or_1 (a_2, and_1_out, and_2_out, and_3_out, and_4_out);
  or or_2 (b_2, and_5_out, and_6_out, and_7_out, and_8_out);
  or or_3 (c_2, and_9_out, and_10_out, and_11_out, and_12_out);
  or or_4 (d_2, and_13_out, and_14_out, and_15_out, and_16_out);
  or or_5 (e, and_17_out, and_18_out);
  or or_6 (f, and_19_out, and_20_out, and_21_out, and_22_out);
  or or_7 (g, and_23_out, and_24_out, and_25_out, and_26_out);
endmodule

module _7_segmentos_full (
  input  A,
  input  B,
  input  C,
  input  D,
  output a_2,
  output b_2,
  output c_2,
  output d_2,
  output e,
  output f,
  output g
);

  wire and_1_out, and_2_out, and_3_out, and_4_out, and_5_out, and_6_out, and_7_out, and_8_out, and_9_out,
       and_10_out, and_11_out, and_12_out, and_13_out, and_14_out, and_15_out, and_16_out, and_17_out,
       and_18_out, and_19_out, and_20_out, and_21_out, and_22_out, and_23_out, and_24_out, and_25_out,
       and_26_out, and_27_out, and_28_out, and_29_out, and_30_out, and_31_out, and_32_out, and_33_out,
       and_34_out, and_35_out;

  and and_1 (and_1_out, A, ~B, ~C);  // AND_Gate
  and and_2 (and_2_out, ~A, B, D);  // AND_Gate
  and and_3 (and_3_out, A, ~D);  // AND_Gate
  and and_4 (and_4_out, ~A, C);  // AND_Gate
  and and_5 (and_5_out, B, C);
  and and_6 (and_6_out, ~B, ~D);  // AND_Gate
  and and_7 (and_7_out, ~A, ~C, ~D);  // AND_Gate
  and and_8 (and_8_out, ~A, C, D);  // AND_Gate
  and and_9 (and_9_out, A, ~C, D);  // AND_Gate
  and and_10 (and_10_out, ~B, ~C);  // AND_Gate
  and and_11 (and_11_out, ~B, ~D);  // AND_Gate
  and and_12 (and_12_out, ~A, ~C);  // AND_Gate
  and and_13 (and_13_out, ~A, D);  // AND_Gate
  and and_14 (and_14_out, ~C, D);  // AND_Gate
  and and_15 (and_15_out, ~A, B);  // AND_Gate
  and and_16 (and_16_out, A, ~B);  // AND_Gate
  and and_17 (and_17_out, ~A, ~B, ~D);  // AND_Gate
  and and_18 (and_18_out, ~B, C, D);  // AND_Gate
  and and_19 (and_19_out, B, ~C, D);  // AND_Gate
  and and_20 (and_20_out, B, C, ~D);  // AND_Gate
  and and_21 (and_21_out, A, ~C);  // AND_Gate
  and and_22 (and_22_out, ~B, ~D);  // AND_Gate
  and and_23 (and_23_out, C, ~D);  // AND_Gate
  and and_24 (and_24_out, A, C);
  and and_25 (and_25_out, A, B);
  and and_26 (and_26_out, ~A, B, ~C);  // AND_Gate
  and and_27 (and_27_out, ~C, ~D);  // AND_Gate
  and and_28 (and_28_out, B, ~D);  // AND_Gate
  and and_29 (and_29_out, A, ~B);  // AND_Gate
  and and_30 (and_30_out, A, C);
  and and_31 (and_31_out, ~A, B, ~C);  // AND_Gate
  and and_32 (and_32_out, ~B, C);  // AND_Gate
  and and_33 (and_33_out, C, ~D);  // AND_Gate
  and and_34 (and_34_out, A, ~B);  // AND_Gate
  and and_35 (and_35_out, A, D);
  or or_1 (c_2, and_12_out, and_13_out, and_14_out, and_15_out, and_16_out);
  or or_2 (d_2, and_17_out, and_18_out, and_19_out, and_20_out, and_21_out);
  or or_3 (e, and_22_out, and_23_out, and_24_out, and_25_out);
  or or_4 (f, and_26_out, and_27_out, and_28_out, and_29_out, and_30_out);
  or or_5 (g, and_31_out, and_32_out, and_33_out, and_34_out, and_35_out);
  or or_6 (a_2, and_1_out, and_2_out, and_3_out, and_4_out, and_5_out, and_6_out);
  or or_7 (b_2, and_7_out, and_8_out, and_9_out, and_10_out, and_11_out);
endmodule
